// Logisim project main.circ as structural Verilog: 3 circuits, main circuit Full adder (naive)
module Full_adder__naive (
  input  X1,
  input  X2,
  input  Carry,
  output Out,
  output Carry_2
);

  wire and_1_out, and_2_out, and_3_out, and_4_out, and_5_out, and_6_out, and_7_out, not_1_out, not_2_out,
       not_3_out, not_4_out, not_5_out, not_6_out;

  not not_1 (not_1_out, X1);
  not not_2 (not_2_out, X2);
  not not_3 (not_3_out, X1);
  not not_4 (not_4_out, Carry);
  not not_5 (not_5_out, X2);
  not not_6 (not_6_out, Carry);
  and and_1 (and_1_out, not_1_out, not_2_out, Carry);
  and and_2 (and_2_out, not_3_out, X2, not_4_out);
  and and_3 (and_3_out, X1, not_5_out, not_6_out);
  and and_4 (and_4_out, X1, X2, Carry);
  and and_5 (and_5_out, X2, Carry);
  or or_1 (Carry_2, and_5_out, and_6_out, and_7_out);
  and and_6 (and_6_out, X1, Carry);
  and and_7 (and_7_out, X1, X2);
  or or_2 (Out, and_1_out, and_2_out, and_3_out, and_4_out);
endmodule

module _8_bit_summator__beautiful (
  input  [7:0] in_1,
  input  [7:0] in_2,
  input  Carry_In,
  output [7:0] out_4
);

  wire full_adder_naive_1_carry_2, full_adder_naive_2_carry_2, full_adder_naive_3_carry_2,
       full_adder_naive_4_carry_2, full_adder_naive_5_carry_2, full_adder_naive_6_carry_2,
       full_adder_naive_7_carry_2, full_adder_naive_8_carry_2;

  // Probe on full_adder_naive_8_carry_2
  Full_adder__naive full_adder_naive_1 (
    .X1(in_2[0]), .X2(in_1[0]), .Carry(Carry_In), .Out(out_4[0]), .Carry_2(full_adder_naive_1_carry_2));
  Full_adder__naive full_adder_naive_2 (
    .X1(in_2[1]), .X2(in_1[1]), .Carry(full_adder_naive_1_carry_2), .Out(out_4[1]),
    .Carry_2(full_adder_naive_2_carry_2));
  Full_adder__naive full_adder_naive_3 (
    .X1(in_2[2]), .X2(in_1[2]), .Carry(full_adder_naive_2_carry_2), .Out(out_4[2]),
    .Carry_2(full_adder_naive_3_carry_2));
  Full_adder__naive full_adder_naive_4 (
    .X1(in_2[3]), .X2(in_1[3]), .Carry(full_adder_naive_3_carry_2), .Out(out_4[3]),
    .Carry_2(full_adder_naive_4_carry_2));
  Full_adder__naive full_adder_naive_5 (
    .X1(in_2[5]), .X2(in_1[5]), .Carry(full_adder_naive_6_carry_2), .Out(out_4[5]),
    .Carry_2(full_adder_naive_5_carry_2));
  Full_adder__naive full_adder_naive_6 (
    .X1(in_2[4]), .X2(in_1[4]), .Carry(full_adder_naive_4_carry_2), .Out(out_4[4]),
    .Carry_2(full_adder_naive_6_carry_2));
  Full_adder__naive full_adder_naive_7 (
    .X1(in_2[6]), .X2(in_1[6]), .Carry(full_adder_naive_5_carry_2), .Out(out_4[6]),
    .Carry_2(full_adder_naive_7_carry_2));
  Full_adder__naive full_adder_naive_8 (
    .X1(in_2[7]), .X2(in_1[7]), .Carry(full_adder_naive_7_carry_2), .Out(out_4[7]),
    .Carry_2(full_adder_naive_8_carry_2));
endmodule

module BCD_8421_to_8421_5 (
  input  X1,
  input  X2,
  input  X3,
  input  X4,
  output O1,
  output O2,
  output O3,
  output O4
);

  wire and_1_out, and_2_out, and_3_out, and_4_out, and_5_out, and_6_out, and_7_out, and_8_out, and_9_out,
       and_10_out, and_11_out, not_1_out, not_2_out, not_3_out, not_4_out, not_5_out, not_6_out, not_7_out,
       not_8_out, not_9_out, not_10_out, not_11_out, not_12_out, not_13_out, not_14_out, not_15_out,
       not_16_out, not_17_out, not_18_out, not_19_out, not_20_out, not_21_out, not_22_out, not_23_out,
       not_24_out, not_25_out, not_26_out, not_27_out;

  not not_1 (not_1_out, X1);
  not not_2 (not_2_out, X2);
  not not_3 (not_3_out, X1);
  not not_4 (not_4_out, X3);
  not not_5 (not_5_out, X4);
  not not_6 (not_6_out, X2);
  not not_7 (not_7_out, X3);
  not not_8 (not_8_out, X1);
  and and_1 (and_1_out, not_8_out, not_9_out, not_10_out);
  not not_9 (not_9_out, X2);
  not not_10 (not_10_out, X4);
  not not_11 (not_11_out, X2);
  and and_2 (and_2_out, not_11_out, not_12_out, X4);
  not not_12 (not_12_out, X3);
  not not_13 (not_13_out, X1);
  not not_14 (not_14_out, X2);
  not not_15 (not_15_out, X3);
  not not_16 (not_16_out, X1);
  not not_17 (not_17_out, X2);
  not not_18 (not_18_out, X4);
  not not_19 (not_19_out, X1);
  not not_20 (not_20_out, X2);
  not not_21 (not_21_out, X3);
  not not_22 (not_22_out, X4);
  not not_23 (not_23_out, X2);
  and and_3 (and_3_out, not_23_out, not_24_out, not_25_out);
  not not_24 (not_24_out, X3);
  not not_25 (not_25_out, X4);
  not not_26 (not_26_out, X1);
  and and_4 (and_4_out, not_26_out, not_27_out);
  not not_27 (not_27_out, X4);
  and and_5 (and_5_out, not_1_out, not_2_out, X3, X4);
  or or_1 (O1, and_5_out, and_6_out, and_7_out);
  and and_6 (and_6_out, not_3_out, X2, not_4_out, not_5_out);
  and and_7 (and_7_out, X1, not_6_out, not_7_out, X4);
  or or_2 (O2, and_1_out, and_2_out);
  and and_8 (and_8_out, not_13_out, not_14_out, not_15_out, X4);
  and and_9 (and_9_out, not_16_out, not_17_out, X3, not_18_out);
  and and_10 (and_10_out, not_19_out, X2, X3, X4);
  and and_11 (and_11_out, X1, not_20_out, not_21_out, not_22_out);
  or or_3 (O4, and_3_out, and_4_out);
  or or_4 (O3, and_8_out, and_9_out, and_10_out, and_11_out);
endmodule
